// Logisim project Task3.circ as structural Verilog: 1 circuit, main circuit main
module main (
  input  in_1,
  input  in_2
);

  wire and_1_out, and_2_out, and_3_out, and_4_out, and_5_out, and_6_out, and_7_out, and_8_out, and_9_out,
       and_10_out, and_11_out, and_12_out, and_13_out, and_14_out, and_15_out, and_16_out, and_17_out,
       and_18_out, and_19_out, and_20_out, and_21_out, and_22_out, and_23_out, and_24_out, and_25_out,
       and_26_out, and_27_out, and_28_out, and_29_out, and_30_out, and_31_out, and_32_out, and_33_out,
       and_34_out, and_35_out, or_2_out, or_3_out, or_4_out, or_5_out, or_6_out, or_7_out, or_8_out,
       or_9_out, or_10_out, xor_1_out, xor_3_out, xor_4_out, xor_5_out, xor_7_out, xor_8_out, xor_9_out,
       xor_10_out, xor_12_out, xor_13_out, xor_14_out, xor_15_out, xor_17_out, xor_18_out;
  wire [3:0] and_36_out, slider_1_out, slider_2_out, xor_11_out;

  or or_1 (xor_11_out[3], and_2_out, and_3_out);
  and and_1 (and_1_out, slider_1_out[3], slider_2_out[3]);
  and and_2 (and_2_out, and_1_out, or_2_out);
  and and_3 (and_3_out, xor_1_out, or_3_out);
  xor xor_1 (xor_1_out, and_1_out, or_2_out);
  xor xor_2 (xor_11_out[2], xor_1_out, or_3_out);
  Slider #(.width(4)) slider_1 (.out(slider_1_out));
  Slider #(.width(4)) slider_2 (.out(slider_2_out));
  and and_4 (and_4_out, slider_1_out[3], slider_2_out[2]);
  and and_5 (and_5_out, xor_3_out, or_4_out);
  or or_2 (or_2_out, and_8_out, and_5_out);
  and and_6 (and_6_out, slider_1_out[2], slider_2_out[3]);
  and and_7 (and_7_out, xor_4_out, or_5_out);
  or or_3 (or_3_out, and_9_out, and_7_out);
  Hex_Digit_Display hex_digit_display_1 (.value(slider_1_out));  // open: dp
  Hex_Digit_Display hex_digit_display_2 (.value(slider_2_out));  // open: dp
  and and_8 (and_8_out, and_4_out, and_11_out);
  xor xor_3 (xor_3_out, and_4_out, and_11_out);
  and and_9 (and_9_out, and_6_out, xor_5_out);
  xor xor_4 (xor_4_out, and_6_out, xor_5_out);
  xor xor_5 (xor_5_out, xor_3_out, or_4_out);
  xor xor_6 (xor_11_out[1], xor_4_out, or_5_out);
  and and_10 (and_10_out, slider_1_out[3], slider_2_out[1]);
  and and_11 (and_11_out, and_10_out, or_6_out);
  and and_12 (and_12_out, slider_1_out[2], slider_2_out[2]);
  and and_13 (and_13_out, xor_7_out, or_7_out);
  or or_4 (or_4_out, and_16_out, and_13_out);
  and and_14 (and_14_out, slider_1_out[1], slider_2_out[3]);
  and and_15 (and_15_out, xor_8_out, or_8_out);
  or or_5 (or_5_out, and_17_out, and_15_out);
  and and_16 (and_16_out, and_12_out, xor_9_out);
  xor xor_7 (xor_7_out, and_12_out, xor_9_out);
  and and_17 (and_17_out, and_14_out, xor_10_out);
  xor xor_8 (xor_8_out, and_14_out, xor_10_out);
  xor xor_9 (xor_9_out, and_10_out, or_6_out);
  xor xor_10 (xor_10_out, xor_7_out, or_7_out);
  xor xor_11 (xor_11_out[0], xor_8_out, or_8_out);
  and and_18 (and_18_out, slider_1_out[2], slider_2_out[1]);
  and and_19 (and_19_out, and_18_out, and_26_out);
  and and_20 (and_20_out, xor_12_out, or_9_out);
  or or_6 (or_6_out, and_19_out, and_20_out);
  and and_21 (and_21_out, slider_1_out[1], slider_2_out[2]);
  and and_22 (and_22_out, and_21_out, xor_13_out);
  and and_23 (and_23_out, xor_14_out, or_10_out);
  or or_7 (or_7_out, and_22_out, and_23_out);
  and and_24 (and_24_out, slider_1_out[0], slider_2_out[3]);
  and and_25 (and_25_out, and_24_out, xor_15_out);
  or or_8 (or_8_out, and_25_out, in_2);
  and and_26 (and_26_out, slider_1_out[3], slider_2_out[0]);
  xor xor_12 (xor_12_out, and_18_out, and_26_out);
  xor xor_13 (xor_13_out, xor_12_out, or_9_out);
  xor xor_14 (xor_14_out, and_21_out, xor_13_out);
  xor xor_15 (xor_15_out, xor_14_out, or_10_out);
  xor xor_16 (and_36_out[3], and_24_out, xor_15_out);
  and and_27 (and_27_out, slider_1_out[1], slider_2_out[1]);
  and and_28 (and_28_out, and_27_out, and_32_out);
  and and_29 (and_29_out, xor_17_out, and_34_out);
  or or_9 (or_9_out, and_28_out, and_29_out);
  and and_30 (and_30_out, slider_1_out[0], slider_2_out[2]);
  and and_31 (and_31_out, and_30_out, xor_18_out);
  or or_10 (or_10_out, and_31_out, in_1);
  and and_32 (and_32_out, slider_1_out[2], slider_2_out[0]);
  xor xor_17 (xor_17_out, and_27_out, and_32_out);
  xor xor_18 (xor_18_out, xor_17_out, and_34_out);
  xor xor_19 (and_36_out[2], and_30_out, xor_18_out);
  and and_33 (and_33_out, slider_1_out[0], slider_2_out[1]);
  and and_34 (and_34_out, and_33_out, and_35_out);
  and and_35 (and_35_out, slider_1_out[1], slider_2_out[0]);
  xor xor_20 (and_36_out[1], and_33_out, and_35_out);
  and and_36 (and_36_out[0], slider_1_out[0], slider_2_out[0]);
  Hex_Digit_Display hex_digit_display_3 (.value(xor_11_out));  // open: dp
  Hex_Digit_Display hex_digit_display_4 (.value(and_36_out));  // open: dp

  // Notes on the sheet:
  //   A4
  //   B
  //   A
  //   A4
  //   A3
  //   A4
  //   A3
  //   A2
  //   A3
  //   A2
  //   A1
  //   A2
  //   A1
  //   A1
endmodule
