// Logisim project Task4.circ as structural Verilog: 1 circuit, main circuit main
module main (
  input  P
);

  wire and_17_out, and_18_out, and_19_out, and_20_out, and_21_out, and_22_out, and_23_out, and_24_out,
       and_25_out, and_26_out, and_27_out, and_28_out, and_29_out, and_30_out, P0C_out, P1C_out;
  wire [1:0] slider_3_out, slider_3_out_2, slider_3_out_3, slider_3_out_4, slider_3_out_5, slider_3_out_6,
       slider_3_out_7, slider_3_out_8, slider_4_out, slider_4_out_2, slider_4_out_3, slider_4_out_4,
       slider_4_out_5, slider_4_out_6, slider_4_out_7, slider_4_out_8;
  wire [3:0] xor_5_out, xor_8_out, xor_12_out, xor_18_out;
  wire [15:0] and_16_out, C0_out, xor_32_out;

  Hex_Digit_Display hex_digit_display_1 (.value({slider_4_out_8[1], slider_4_out_7[1], slider_4_out_6[1], slider_4_out_5[1]}));  // open: dp
  Hex_Digit_Display hex_digit_display_2 (.value({slider_4_out_8[0], slider_4_out_7[0], slider_4_out_6[0], slider_4_out_5[0]}));  // open: dp
  Hex_Digit_Display hex_digit_display_3 (.value(xor_5_out));  // open: dp
  Hex_Digit_Display hex_digit_display_4 (.value({slider_4_out_4[1], slider_4_out_3[1], slider_4_out_2[1], slider_4_out[1]}));  // open: dp
  Hex_Digit_Display hex_digit_display_5 (.value({slider_3_out_7[1], slider_3_out_6[1], slider_3_out_5[1], slider_3_out_4[1]}));  // open: dp
  Hex_Digit_Display hex_digit_display_6 (.value({slider_4_out_4[0], slider_4_out_3[0], slider_4_out_2[0], slider_4_out[0]}));  // open: dp
  Hex_Digit_Display hex_digit_display_7 (.value({slider_3_out_7[0], slider_3_out_6[0], slider_3_out_5[0], slider_3_out_4[0]}));  // open: dp
  Hex_Digit_Display hex_digit_display_8 (.value(xor_8_out));  // open: dp
  Hex_Digit_Display hex_digit_display_9 (.value({slider_3_out_3[1], slider_3_out_2[1], slider_3_out[1], slider_3_out_8[1]}));  // open: dp
  Hex_Digit_Display hex_digit_display_10 (.value({slider_3_out_3[0], slider_3_out_2[0], slider_3_out[0], slider_3_out_8[0]}));  // open: dp
  Hex_Digit_Display hex_digit_display_11 (.value(xor_12_out));  // open: dp
  Hex_Digit_Display hex_digit_display_12 (.value(xor_18_out));  // open: dp
  Slider slider_1 (.out({slider_3_out_7[1], slider_3_out_6[1], slider_3_out_5[1], slider_3_out_4[1], slider_3_out_3[1], slider_3_out_2[1], slider_3_out[1], slider_3_out_8[1]}));
  Slider slider_2 (.out({slider_4_out_8[1], slider_4_out_7[1], slider_4_out_6[1], slider_4_out_5[1], slider_4_out_4[1], slider_4_out_3[1], slider_4_out_2[1], slider_4_out[1]}));
  Slider slider_3 (.out({slider_3_out_7[0], slider_3_out_6[0], slider_3_out_5[0], slider_3_out_4[0], slider_3_out_3[0], slider_3_out_2[0], slider_3_out[0], slider_3_out_8[0]}));
  Slider slider_4 (.out({slider_4_out_8[0], slider_4_out_7[0], slider_4_out_6[0], slider_4_out_5[0], slider_4_out_4[0], slider_4_out_3[0], slider_4_out_2[0], slider_4_out[0]}));
  and and_1 (and_16_out[15], slider_4_out_8[1], slider_4_out_8[0]);
  and and_2 (and_16_out[14], slider_4_out_7[1], slider_4_out_7[0]);
  xor xor_1 (xor_5_out[3], xor_32_out[15], C0_out[14]);
  and and_3 (and_16_out[13], slider_4_out_6[1], slider_4_out_6[0]);
  and and_4 (and_16_out[12], slider_4_out_5[1], slider_4_out_5[0]);
  xor xor_2 (xor_5_out[2], xor_32_out[14], C0_out[13]);
  and and_5 (and_16_out[11], slider_4_out_4[1], slider_4_out_4[0]);
  xor xor_3 (xor_5_out[1], xor_32_out[13], C0_out[12]);
  and and_6 (and_16_out[10], slider_4_out_3[1], slider_4_out_3[0]);
  xor xor_4 (xor_8_out[3], xor_32_out[11], C0_out[10]);
  xor xor_5 (xor_5_out[0], xor_32_out[12], C0_out[11]);
  and and_7 (and_16_out[9], slider_4_out_2[1], slider_4_out_2[0]);
  and and_8 (and_16_out[8], slider_4_out[1], slider_4_out[0]);
  xor xor_6 (xor_8_out[2], xor_32_out[10], C0_out[9]);
  and and_9 (and_16_out[7], slider_3_out_7[1], slider_3_out_7[0]);
  xor xor_7 (xor_8_out[1], xor_32_out[9], C0_out[8]);
  and and_10 (and_16_out[6], slider_3_out_6[1], slider_3_out_6[0]);
  xor xor_8 (xor_8_out[0], xor_32_out[8], C0_out[7]);
  xor xor_9 (xor_12_out[3], xor_32_out[7], C0_out[6]);
  and and_11 (and_16_out[5], slider_3_out_5[1], slider_3_out_5[0]);
  and and_12 (and_16_out[4], slider_3_out_4[1], slider_3_out_4[0]);
  xor xor_10 (xor_12_out[2], xor_32_out[6], C0_out[5]);
  and and_13 (and_16_out[3], slider_3_out_3[1], slider_3_out_3[0]);
  xor xor_11 (xor_12_out[1], xor_32_out[5], C0_out[4]);
  and and_14 (and_16_out[2], slider_3_out_2[1], slider_3_out_2[0]);
  xor xor_12 (xor_12_out[0], xor_32_out[4], C0_out[3]);
  xor xor_13 (xor_18_out[3], xor_32_out[3], C0_out[2]);
  and and_15 (and_16_out[1], slider_3_out[1], slider_3_out[0]);
  and and_16 (and_16_out[0], slider_3_out_8[1], slider_3_out_8[0]);
  xor xor_14 (xor_18_out[2], xor_32_out[2], C0_out[1]);
  xor xor_15 (xor_18_out[1], xor_32_out[1], C0_out[0]);
  xor xor_16 (xor_32_out[15], slider_4_out_8[1], slider_4_out_8[0]);
  xor xor_17 (xor_32_out[14], slider_4_out_7[1], slider_4_out_7[0]);
  or or_1 (C0_out[15], and_16_out[15], and_17_out);
  xor xor_18 (xor_18_out[0], xor_32_out[0], P);
  xor xor_19 (xor_32_out[13], slider_4_out_6[1], slider_4_out_6[0]);
  and and_17 (and_17_out, xor_32_out[15], C0_out[14]);
  or or_2 (C0_out[14], and_16_out[14], and_18_out);
  xor xor_20 (xor_32_out[12], slider_4_out_5[1], slider_4_out_5[0]);
  and and_18 (and_18_out, xor_32_out[14], C0_out[13]);
  or or_3 (C0_out[13], and_16_out[13], and_19_out);
  xor xor_21 (xor_32_out[11], slider_4_out_4[1], slider_4_out_4[0]);
  xor xor_22 (xor_32_out[10], slider_4_out_3[1], slider_4_out_3[0]);
  and and_19 (and_19_out, xor_32_out[13], C0_out[12]);
  or or_4 (C0_out[12], and_16_out[12], and_20_out);
  xor xor_23 (xor_32_out[9], slider_4_out_2[1], slider_4_out_2[0]);
  and and_20 (and_20_out, xor_32_out[12], C0_out[11]);
  or or_5 (C0_out[11], and_16_out[11], and_21_out);
  xor xor_24 (xor_32_out[8], slider_4_out[1], slider_4_out[0]);
  and and_21 (and_21_out, xor_32_out[11], C0_out[10]);
  or or_6 (C0_out[10], and_16_out[10], and_22_out);
  xor xor_25 (xor_32_out[7], slider_3_out_7[1], slider_3_out_7[0]);
  xor xor_26 (xor_32_out[6], slider_3_out_6[1], slider_3_out_6[0]);
  and and_22 (and_22_out, xor_32_out[10], C0_out[9]);
  or or_7 (C0_out[9], and_16_out[9], and_23_out);
  xor xor_27 (xor_32_out[5], slider_3_out_5[1], slider_3_out_5[0]);
  and and_23 (and_23_out, xor_32_out[9], C0_out[8]);
  or or_8 (C0_out[8], and_16_out[8], and_24_out);
  xor xor_28 (xor_32_out[4], slider_3_out_4[1], slider_3_out_4[0]);
  and and_24 (and_24_out, xor_32_out[8], C0_out[7]);
  or or_9 (C0_out[7], and_16_out[7], and_25_out);
  xor xor_29 (xor_32_out[3], slider_3_out_3[1], slider_3_out_3[0]);
  xor xor_30 (xor_32_out[2], slider_3_out_2[1], slider_3_out_2[0]);
  and and_25 (and_25_out, xor_32_out[7], C0_out[6]);
  or or_10 (C0_out[6], and_16_out[6], and_26_out);
  xor xor_31 (xor_32_out[1], slider_3_out[1], slider_3_out[0]);
  and and_26 (and_26_out, xor_32_out[6], C0_out[5]);
  or or_11 (C0_out[5], and_16_out[5], and_27_out);
  xor xor_32 (xor_32_out[0], slider_3_out_8[1], slider_3_out_8[0]);
  and and_27 (and_27_out, xor_32_out[5], C0_out[4]);
  or or_12 (C0_out[4], and_16_out[4], and_28_out);
  and and_28 (and_28_out, xor_32_out[4], C0_out[3]);
  or or_13 (C0_out[3], and_16_out[3], and_29_out);
  and and_29 (and_29_out, xor_32_out[3], C0_out[2]);
  or or_14 (C0_out[2], and_16_out[2], and_30_out);
  and and_30 (and_30_out, xor_32_out[2], C0_out[1]);
  or C1 (C0_out[1], and_16_out[1], P1C_out);
  and P1C (P1C_out, xor_32_out[1], C0_out[0]);
  or C0 (C0_out[0], and_16_out[0], P0C_out);
  and P0C (P0C_out, xor_32_out[0], P);

  // Notes on the sheet:
  //   A
  //   B
  //   G = AB
  //   A
  //   B
  //   P
  //   Ci=Pi*C(i-1)+Gi
  //   P = A⊕B
  //   G = AB
endmodule
