// Logisim project Task1.circ as structural Verilog: 1 circuit, main circuit main
module main (
);

  wire button_1_out, button_2_out, t_ff_1_qn, t_ff_3_qn, t_ff_5_qn;
  wire [3:0] t_ff_1_q, t_ff_2_q;

  T_Flip_Flop t_ff_1 (.T(1'b1), .clk(button_1_out), .Q(t_ff_1_q[0]), .Qn(t_ff_1_qn));  // open: reset, preset
  Button button_1 (.out(button_1_out));
  T_Flip_Flop t_ff_2 (.T(1'b1), .clk(button_2_out), .Q(t_ff_2_q[0]));  // open: Qn, reset, preset
  Button button_2 (.out(button_2_out));
  T_Flip_Flop t_ff_3 (.T(1'b1), .clk(t_ff_1_qn), .Q(t_ff_1_q[1]), .Qn(t_ff_3_qn));  // open: reset, preset
  T_Flip_Flop t_ff_4 (.T(1'b1), .clk(t_ff_2_q[0]), .Q(t_ff_2_q[1]));  // open: Qn, reset, preset
  T_Flip_Flop t_ff_5 (.T(1'b1), .clk(t_ff_3_qn), .Q(t_ff_1_q[2]), .Qn(t_ff_5_qn));  // open: reset, preset
  T_Flip_Flop t_ff_6 (.T(1'b1), .clk(t_ff_2_q[1]), .Q(t_ff_2_q[2]));  // open: Qn, reset, preset
  T_Flip_Flop t_ff_7 (.T(1'b1), .clk(t_ff_5_qn), .Q(t_ff_1_q[3]));  // open: Qn, reset, preset
  T_Flip_Flop t_ff_8 (.T(1'b1), .clk(t_ff_2_q[2]), .Q(t_ff_2_q[3]));  // open: Qn, reset, preset
  Hex_Digit_Display hex_digit_display_1 (.value(t_ff_1_q));  // open: dp
  Hex_Digit_Display hex_digit_display_2 (.value(t_ff_2_q));  // open: dp
endmodule
