// Logisim project Task2.circ as structural Verilog: 1 circuit, main circuit main
module main (
);

  wire and_1_out, button_1_out, t_ff_1_qn, t_ff_2_qn, t_ff_3_qn;
  wire [3:0] t_ff_1_q;

  T_Flip_Flop t_ff_1 (
    .T(1'b1), .clk(button_1_out), .Q(t_ff_1_q[0]), .Qn(t_ff_1_qn), .reset(and_1_out));  // open: preset
  Button button_1 (.out(button_1_out));
  T_Flip_Flop t_ff_2 (.T(1'b1), .clk(t_ff_1_qn), .Q(t_ff_1_q[1]), .Qn(t_ff_2_qn), .reset(and_1_out));  // open: preset
  T_Flip_Flop t_ff_3 (.T(1'b1), .clk(t_ff_2_qn), .Q(t_ff_1_q[2]), .Qn(t_ff_3_qn), .reset(and_1_out));  // open: preset
  T_Flip_Flop t_ff_4 (.T(1'b1), .clk(t_ff_3_qn), .Q(t_ff_1_q[3]), .reset(and_1_out));  // open: Qn, preset
  and and_1 (and_1_out, t_ff_1_qn, t_ff_1_q[1], t_ff_3_qn, t_ff_1_q[3]);
  Hex_Digit_Display hex_digit_display_1 (.value(t_ff_1_q));  // open: dp
endmodule
