// Logisim project Task3.circ as structural Verilog: 1 circuit, main circuit main
module main (
);

  wire and_1_out, button_1_out, t_ff_1_qn, t_ff_2_qn, t_ff_3_qn, xnor_1_out, xnor_2_out, xnor_3_out,
       xnor_4_out;
  wire [3:0] slider_1_out, t_ff_1_q;

  T_Flip_Flop t_ff_1 (
    .T(1'b1), .clk(button_1_out), .Q(t_ff_1_q[0]), .Qn(t_ff_1_qn), .reset(and_1_out));  // open: preset
  Button button_1 (.out(button_1_out));
  and and_1 (and_1_out, xnor_4_out, xnor_3_out, xnor_2_out, xnor_1_out);
  xnor xnor_1 (xnor_1_out, t_ff_1_q[0], slider_1_out[0]);
  xnor xnor_2 (xnor_2_out, t_ff_1_q[1], slider_1_out[1]);
  xnor xnor_3 (xnor_3_out, t_ff_1_q[2], slider_1_out[2]);
  xnor xnor_4 (xnor_4_out, t_ff_1_q[3], slider_1_out[3]);
  T_Flip_Flop t_ff_2 (.T(1'b1), .clk(t_ff_1_qn), .Q(t_ff_1_q[1]), .Qn(t_ff_2_qn), .reset(and_1_out));  // open: preset
  T_Flip_Flop t_ff_3 (.T(1'b1), .clk(t_ff_2_qn), .Q(t_ff_1_q[2]), .Qn(t_ff_3_qn), .reset(and_1_out));  // open: preset
  T_Flip_Flop t_ff_4 (.T(1'b1), .clk(t_ff_3_qn), .Q(t_ff_1_q[3]), .reset(and_1_out));  // open: Qn, preset
  Hex_Digit_Display hex_digit_display_1 (.value(slider_1_out));  // open: dp
  Slider #(.width(4)) slider_1 (.out(slider_1_out));
  Hex_Digit_Display hex_digit_display_2 (.value(t_ff_1_q));  // open: dp
endmodule
