// Logisim project Task4.circ as structural Verilog: 1 circuit, main circuit main
module main (
);

  wire and_1_out, button_1_out, d_ff_1_qn, d_ff_2_qn, d_ff_3_qn, d_ff_4_qn, xnor_1_out, xnor_2_out,
       xnor_3_out, xnor_4_out;
  wire [3:0] d_ff_1_q, slider_1_out;

  Button button_1 (.out(button_1_out));
  D_Flip_Flop d_ff_1 (
    .D(d_ff_1_qn), .clk(button_1_out), .Q(d_ff_1_q[0]), .Qn(d_ff_1_qn), .reset(and_1_out));  // open: preset
  and and_1 (and_1_out, xnor_4_out, xnor_3_out, xnor_2_out, xnor_1_out);
  xnor xnor_1 (xnor_1_out, d_ff_1_q[0], slider_1_out[0]);
  xnor xnor_2 (xnor_2_out, d_ff_1_q[1], slider_1_out[1]);
  xnor xnor_3 (xnor_3_out, d_ff_1_q[2], slider_1_out[2]);
  xnor xnor_4 (xnor_4_out, d_ff_1_q[3], slider_1_out[3]);
  D_Flip_Flop d_ff_2 (
    .D(d_ff_2_qn), .clk(d_ff_1_qn), .Q(d_ff_1_q[1]), .Qn(d_ff_2_qn), .reset(and_1_out));  // open: preset
  D_Flip_Flop d_ff_3 (
    .D(d_ff_3_qn), .clk(d_ff_2_qn), .Q(d_ff_1_q[2]), .Qn(d_ff_3_qn), .reset(and_1_out));  // open: preset
  D_Flip_Flop d_ff_4 (
    .D(d_ff_4_qn), .clk(d_ff_3_qn), .Q(d_ff_1_q[3]), .Qn(d_ff_4_qn), .reset(and_1_out));  // open: preset
  Hex_Digit_Display hex_digit_display_1 (.value(slider_1_out));  // open: dp
  Slider #(.width(4)) slider_1 (.out(slider_1_out));
  Hex_Digit_Display hex_digit_display_2 (.value(d_ff_1_q));  // open: dp
endmodule
