// Logisim project Task5.circ as structural Verilog: 1 circuit, main circuit main
module main (
);

  wire and_1_out, button_1_out, not_1_out, t_ff_1_qn, t_ff_2_qn, t_ff_3_qn, t_ff_4_qn, xor_1_out;
  wire [3:0] t_ff_1_q;

  Button button_1 (.out(button_1_out));
  T_Flip_Flop t_ff_1 (
    .T(1'b1), .clk(button_1_out), .Q(t_ff_1_q[0]), .Qn(t_ff_1_qn), .reset(and_1_out));  // open: preset
  and and_1 (and_1_out, not_1_out, t_ff_4_qn, t_ff_3_qn, t_ff_1_q[1], t_ff_1_qn);
  not not_1 (not_1_out, button_1_out);
  T_Flip_Flop t_ff_2 (.T(1'b1), .clk(xor_1_out), .Q(t_ff_1_q[1]), .Qn(t_ff_2_qn), .reset(and_1_out));  // open: preset
  xor xor_1 (xor_1_out, t_ff_1_qn, button_1_out);
  T_Flip_Flop t_ff_3 (.T(1'b1), .clk(t_ff_2_qn), .Q(t_ff_1_q[2]), .Qn(t_ff_3_qn), .reset(and_1_out));  // open: preset
  T_Flip_Flop t_ff_4 (.T(1'b1), .clk(t_ff_3_qn), .Q(t_ff_1_q[3]), .Qn(t_ff_4_qn), .reset(and_1_out));  // open: preset
  Hex_Digit_Display hex_digit_display_1 (.value(t_ff_1_q));  // open: dp
endmodule
